# Fritzing sketch esquema Wemos NRF24 (saved by Fritzing 0.9.3b)
breadboards: 1
perfboards: 1

parts:
  J1 = RJ11 Jack [package=rj11-6]
  Part1 = NRF24L01+ Breakout Board
  WeMos_D1_Mini1 = WeMos D1 Mini
  R3 = Resistor [tolerance=±5% resistance=4.7k package=THT]

nets:
  VCC: J1.2, Part1.VCC, WeMos_D1_Mini1.3V3, R3.Pin_0
  N1: J1.4, WeMos_D1_Mini1.D2, R3.Pin_1
  N2: J1.5, Part1.GND, WeMos_D1_Mini1.G
  N3: Part1.CE, WeMos_D1_Mini1.D4
  N4: Part1.CS, WeMos_D1_Mini1.D8
  N5: Part1.SCK, WeMos_D1_Mini1.D5
  N6: Part1.MOSI, WeMos_D1_Mini1.D7
  N7: Part1.MISO, WeMos_D1_Mini1.D6
  N8: WeMos_D1_Mini1.D0, WeMos_D1_Mini1.RST
