# Fritzing sketch esquema Wemos (saved by Fritzing 0.9.3b)
perfboards: 1

parts:
  J1 = RJ11 Jack [package=rj11-6]
  WeMos_D1_Mini1 = WeMos D1 Mini
  R3 = Resistor [tolerance=±5% resistance=4.7k package=THT]

nets:
  3.3V: J1.2, WeMos_D1_Mini1.3V3, R3.Pin_0
  N1: J1.4, WeMos_D1_Mini1.D2, R3.Pin_1
  GND: J1.5, WeMos_D1_Mini1.G
  N2: WeMos_D1_Mini1.D0, WeMos_D1_Mini1.RST
